# Fritzing sketch Fritizingprojarduinofeito (saved by Fritzing 1.0.4)
breadboards: 1

parts:
  PIR1 = PIR sensor
  Part1 = Arduino Uno (Rev3) - ICSP
  DHT1 = Humidity and Temperature Sensor DHT11
  R4 = Photocell (LDR) [package=THT]

nets:
  VDD: PIR1.VDD, Part1.5V, DHT1.Vcc
  N1: PIR1.SIG, Part1.D2
  GND: PIR1.GND, Part1.GND, DHT1.GND_2, R4.pin_1
  N2: Part1.A0, R4.pin_0
  N3: Part1.D4, DHT1.Data-signal

custom parts:
  Humidity and Temperature Sensor DHT11: Digital relative humidity & temperature sensor DHT11
